# Fritzing sketch Pinout_Raspberry_Pi (saved by Fritzing 0.9.6b)
breadboards: 1

parts:
  Raspberry_Pi_1 = Raspberry Pi 3 [part_number=RPI-3-V1.2]
  Part1 = Logic Level Converter

nets:
  N1: Raspberry_Pi_1.3v3, Part1.LV
  GND: Raspberry_Pi_1.GND, Part1.GND
  N2: Raspberry_Pi_1.GIPO15, Part1.TX2_LV

notes:
  Coffee Maker
  JURA Smart Connect
  5V
  GND
  TX
  RX
  Unused
